// Logisim project trabs.circ as structural Verilog: 1 circuit, main circuit main
module main (
  input  in_1,
  input  [7:0] in_2,
  input  [7:0] in_3,
  input  [7:0] in_4,
  input  [7:0] in_5,
  input  [7:0] in_6,
  input  [7:0] in_7,
  input  [7:0] _1000,
  input  [7:0] in_9,
  input  [7:0] _111011,
  input  [7:0] _1001,
  input  [7:0] _110,
  input  [7:0] _1101,
  input  in_14,
  input  in_15,
  input  in_16,
  input  in_17,
  input  in_18,
  input  [2:0] \input ,
  input  [2:0] in_20,
  input  _1_clock_p,
  input  \_1_grava_0_lê ,
  input  contador,
  input  [7:0] in_24,
  input  _1_acrescenta,
  input  \_1º_limpa ,
  input  in_27,
  input  in_28,
  output out_29,
  output out_30,
  output out_31,
  output out_32,
  output out_33
);

  wire buffer_1_out, clock_1_out, controlled_inverter_1_out, not_1_out, not_2_out, not_3_out, or_1_out;
  wire [6:0] rom_1_data;
  wire [7:0] adder_1_out, adder_2_out, adder_3_out, adder_4_out, adder_5_out, controlled_buffer_1_out,
       counter_1_q, multiplexer_1_out, multiplexer_2_out, multiplexer_3_out, multiplexer_4_out,
       multiplexer_5_out, multiplexer_6_out;

  DotMatrix #(.matrixcols(2), .matrixrows(3), .dotshape("circle")) dotmatrix_1 (.col0(\input ), .col1(in_20));
  Clock clock_1 (.out(clock_1_out));
  Multiplexer #(.width(8)) multiplexer_1 (
    .in0(in_2), .in1(_1000), .out(multiplexer_1_out), .sel(\input [2]), .en(in_1));
  Counter counter_1 (
    .load(contador), .D(in_24), .count(_1_acrescenta), .Q(counter_1_q), .clk(or_1_out),
    .clr(controlled_inverter_1_out));  // open: carry
  or or_1 (or_1_out, _1_clock_p, clock_1_out);
  assign controlled_buffer_1_out = \_1_grava_0_lê  ? adder_5_out : 8'bz;  // Controlled_Buffer controlled_buffer_1
  assign controlled_inverter_1_out = in_27 ? ~\_1_grava_0_lê  : 1'bz;  // Controlled_Inverter controlled_inverter_1
  Multiplexer #(.width(8)) multiplexer_2 (.in0(in_3), .in1(in_9), .out(multiplexer_2_out), .sel(\input [1]), .en(in_1));
  buf buffer_1 (buffer_1_out, \_1_grava_0_lê );
  not not_1 (not_1_out, \_1_grava_0_lê );
  Adder adder_1 (.a(multiplexer_2_out), .b(multiplexer_1_out), .out(adder_1_out), .cin(in_18), .cout(out_33));
  RAM #(.bus("asynch")) ram_1 (
    .addr(counter_1_q), .data(controlled_buffer_1_out), .ld(not_1_out), .clr(\_1º_limpa ));  // open: sel
  Multiplexer #(.width(8)) multiplexer_3 (
    .in0(in_4), .in1(_111011), .out(multiplexer_3_out), .sel(\input [0]), .en(in_1));
  Adder adder_2 (.a(multiplexer_3_out), .b(adder_1_out), .out(adder_2_out), .cin(in_15), .cout(out_30));
  Multiplexer #(.width(8)) multiplexer_4 (.in0(in_5), .in1(_1001), .out(multiplexer_4_out), .sel(in_20[2]), .en(in_1));
  Adder adder_3 (.a(multiplexer_4_out), .b(adder_2_out), .out(adder_3_out), .cin(in_16), .cout(out_31));
  not not_2 (not_2_out, or_1_out);
  not not_3 (not_3_out, buffer_1_out);
  Multiplexer #(.width(8)) multiplexer_5 (.in0(in_6), .in1(_110), .out(multiplexer_5_out), .sel(in_20[1]), .en(in_1));
  ROM #(.dataWidth(7)) rom_1 (.addr(controlled_buffer_1_out), .data(rom_1_data), .sel(or_1_out));
  TTY tty_1 (.data(rom_1_data), .clk(not_2_out), .we(not_3_out), .clr(in_28));
  Adder adder_4 (.a(multiplexer_5_out), .b(adder_3_out), .out(adder_4_out), .cin(in_17), .cout(out_32));
  Multiplexer #(.width(8)) multiplexer_6 (.in0(in_7), .in1(_1101), .out(multiplexer_6_out), .sel(in_20[0]), .en(in_1));
  Adder adder_5 (.a(multiplexer_6_out), .b(adder_4_out), .out(adder_5_out), .cin(in_14), .cout(out_29));

  // Notes on the sheet:
  //   inserir
  //   insert text
  //   sempre parar o clock no 0
  //   10001
  //   1- volta p/0 quando tiver no modo leitura
  //   4º de um clock
  //   2º deixa o contador no 0
  //   3ºcoloque o caractere desejado no input
  //   para inserir coloque a entrada no input
  //   1º coloca no modo gravação
  //   1=Lê o caractere 0= não lê
  //   para ler o texto
  //   1ºcoloque no modo leitura
  //   2ºvolte o contador para 0
  //   3ºcrtl k para iniciar o clock
  //   contents of rom_1 (hex, n*v repeats v):
  //   8*0 61 5*0 65 0 0 63 5*0 64 0 62 69 4*0 68 6a 0 66 5*0 67 4*0 77 21*0 6b 5*0 6f 0 0 6d 0 0 0 75 0 6e
  //   0 6c 73 7a 0 0 78 72 74 0 70 0 79 0 76 0 71
  //   Limpa a Saída de texto
  //   deixar no 1 sempre
endmodule
